# Fritzing sketch BadIncLoraRX (saved by Fritzing 0.9.4)

parts:
  U2 = Chip antenna [package=antenna-chip3]
  NEOPIXEL1 = Neopixel Strip -- Black (30/m) [part_number=1376]
  Part1 = Adafruit Feather 32u4 RFM9xW LoRa [part_number="Adafruit #3078 and Adafruit #3079"]
  S1 = Pushbutton [package="[THT]"]

nets:
  N1: U2.SIGNAL, Part1.ANT
  GND: NEOPIXEL1.GND, Part1.GND, S1.Pin_3, S1.Pin_4
  N2: NEOPIXEL1.Din, Part1.6
  N3: NEOPIXEL1.+5V, Part1.VBUS
  N4: Part1.5, S1.Pin_1, S1.Pin_2

notes:
  Необязательная кнопка, будет убрана
  5V Питание
  НЕЛЬЗЯ использовать ВМЕСТЕ с USB кабелем
  (Или одно, или другое)
  На обратной стороне BSFrance надо перерезать перемычку "DIO10->6 default closed"

custom parts:
  Neopixel Strip -- Black (30/m): These NeoPixel strips have 30 digitally-addressable pixel LEDs per meter and are very affordable and are only 12.5 mm wide, 10 mm if you remove the strip from the casing.
  Adafruit Feather 32u4 RFM9xW LoRa: This is the Adafruit Feather 32u4 LoRa Radio (RFM9x) - our take on an microcontroller with a "Long Range (LoRa)" packet radio transceiver with built in USB and battery charging. Its an Adafruit Feather 32u4 with a 868/915 MHz radio module cooked in! Great for making wireless networks that can go further than 2.4GHz 802.15.4 and similar, are more flexible than Bluetooth LE and without the high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
