# Fritzing sketch BadIncLoraTX (saved by Fritzing 0.9.4)

parts:
  U2 = Chip antenna [package=antenna-chip3]
  BsFrance_LoRa32u4 = Adafruit Feather 32u4 RFM9xW LoRa [part_number="Adafruit #3078 and Adafruit #3079"]
  S2 = Pushbutton [package="[THT]"]
  BNO080 = Adafruit BNO085 9-DOF Orientation IMU Fusion [part_number="Addfruit #4754"]
  LED1 = LED - 5mm [color="Red (633nm)" package="5 mm [THT]"]

nets:
  N1: U2.SIGNAL, BsFrance_LoRa32u4.ANT
  GND: BsFrance_LoRa32u4.GND, S2.Pin_3, S2.Pin_4, BNO080.GND, LED1.cathode
  +3V3: BsFrance_LoRa32u4.+3V3, BNO080.3.3V
  N2: BsFrance_LoRa32u4.10, LED1.anode
  N3: BsFrance_LoRa32u4.5, S2.Pin_1, S2.Pin_2
  N4: BsFrance_LoRa32u4.3, BNO080.SCL/SCK/RX
  N5: BsFrance_LoRa32u4.2, BNO080.SDA/MISO/TX

notes:
  5V Питание
  НЕЛЬЗЯ использовать ВМЕСТЕ с USB кабелем
  (Или одно, или другое)
  BNO080 VCC=3.3V !

custom parts:
  Adafruit Feather 32u4 RFM9xW LoRa: This is the Adafruit Feather 32u4 LoRa Radio (RFM9x) - our take on an microcontroller with a "Long Range (LoRa)" packet radio transceiver with built in USB and battery charging. Its an Adafruit Feather 32u4 with a 868/915 MHz radio module cooked in! Great for making wireless networks that can go further than 2.4GHz 802.15.4 and similar, are more flexible than Bluetooth LE and without the high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
